# Fritzing sketch erfinder-weihnachtsbaum-raspi (saved by Fritzing 0.9.3b)
circuit board: 4.49999cm x 5.85211cm
breadboards: 1

parts:
  LED0 = smd LED [color="Yellow (585nm)" package="0805 [SMD]"]
  R0 = Resistor [tolerance=±5% resistance=220 package="0805 [SMD]"]
  LED4 = smd LED [color="Red (633nm)" package="0805 [SMD]"]
  LED3 = smd LED [color="Red (633nm)" package="0805 [SMD]"]
  LED5 = smd LED [color="Red (633nm)" package="0805 [SMD]"]
  LED6 = smd LED [color="Red (633nm)" package="0805 [SMD]"]
  LED1 = smd LED [color="Red (633nm)" package="0805 [SMD]"]
  R2 = Resistor [tolerance=±5% resistance=220 package="0805 [SMD]"]
  R5 = Resistor [tolerance=±5% resistance=220 package="0805 [SMD]"]
  R4 = Resistor [tolerance=±5% resistance=220 package="0805 [SMD]"]
  R1 = Resistor [tolerance=±5% resistance=220 package="0805 [SMD]"]
  R6 = Resistor [tolerance=±5% resistance=220 package="0805 [SMD]"]
  R3 = Resistor [tolerance=±5% resistance=220 package="0805 [SMD]"]
  LED2 = smd LED [color="Red (633nm)" package="0805 [SMD]"]
  IC1 = ATTINY13 [package=so]
  Pad1 = Pad [width=7.168444444444444 height=6.4911111111111088 connect=center]

nets:
  N1: LED0.cathode, LED4.cathode, LED3.cathode, LED5.cathode, LED6.cathode, LED1.cathode, LED2.cathode, IC1.GND, Pad1.pad
  N2: LED0.anode, R0.Pin_0
  N3: R0.Pin_1, IC1.VCC
  N4: LED4.anode, R4.Pin_0
  N5: LED3.anode, R3.Pin_0
  N6: LED5.anode, R5.Pin_0
  N7: LED6.anode, R6.Pin_0
  N8: LED1.anode, R1.Pin_0
  N9: R2.Pin_0, LED2.anode
  N10: R2.Pin_1, IC1.PB3(ADC3)
  N11: R5.Pin_1, IC1.PB1(MISO)
  N12: R4.Pin_1, IC1.PB2(SCK_ADC1)
  N13: R1.Pin_1, IC1.PB4(ADC2)
  N14: R6.Pin_1, IC1.PB0(MOSI)
  N15: R3.Pin_1, IC1.PB5(NRES)
